# Fritzing sketch Sketch (saved by Fritzing 0.9.3b)

parts:
  Part1 = Arduino Uno (Rev3)
  GY2 = MPU-6050 Board GY-521 [form="♀ (female)" package=THT]
  S1 = H-Bridge with L298N
  M1 = DC Motor
  M2 = DC Motor

nets:
  N1: Part1.A4/SDA, GY2.pin4
  N2: Part1.A5/SCL, GY2.pin3
  N3: Part1.D9_PWM, S1.ENA
  N4: Part1.D10_PWM/SS, S1.ENB
  N5: Part1.D2, GY2.pin8
  N6: Part1.D4, S1.IN1
  N7: Part1.D5_PWM, S1.IN2
  N8: Part1.D6_PWM, S1.IN3
  N9: Part1.D7, S1.IN4
  N10: Part1.5V, GY2.pin1
  GND: Part1.GND, GY2.pin2, S1.GND
  N11: S1.M1-01, M2.pin_2
  N12: S1.M1-02, M2.pin_1
  N13: S1.M2-01, M1.pin_2
  N14: S1.M2-02, M1.pin_1

custom parts:
  MPU-6050 Board GY-521: Acelerometro y Giroscopio MPU-6050 Board GY-521
  H-Bridge with L298N: h-bridge

// code stored in the sketch: Sketch2.ino

